# Fritzing sketch Botones (saved by Fritzing 0.8.3b)
perfboards: 1

parts:
  Raspberry_Pi_rev1 = Raspberry Pi rev2
  S1 = Pushbutton [package="[THT]"]
  S2 = Pushbutton [package="[THT]"]
  R1 = Resistor [tolerance=±5% resistance=10k package=THT]
  R2 = Resistor [tolerance=±5% resistance=10k package=THT]

nets:
  N1: Raspberry_Pi_rev1.5V, R1.Pin_0, R2.Pin_1
  N2: Raspberry_Pi_rev1.GND, S1.Pin_3, S1.Pin_4
  N3: Raspberry_Pi_rev1.GPIO_23, S2.Pin_1, S2.Pin_2, R1.Pin_1
  N4: Raspberry_Pi_rev1.GPIO_22, S1.Pin_1, S1.Pin_2, R2.Pin_0
  N5: S2.Pin_3, S2.Pin_4
